# Fritzing sketch Esquema de Ligação Protoboard (saved by Fritzing 0.9.3b)
breadboards: 1

parts:
  T1 = LM35 Temperature Sensor [package="TO92 [THT]"]
  Componente1 = Arduino Mega 2560 (Rev3)
  LED1 = LED - 3mm [color="Infrared (880nm)" package="3 mm [THT]"]
  R1 = Resistor [tolerance=±5% resistance=10 package=THT]
  Componente3 = Arduino Pro Mini v13
  T2 = LM35 Temperature Sensor [package="TO92 [THT]"]
  LED2 = LED - 5mm [color="Infrared (940nm)" package="5 mm [THT]"]
  R2 = Resistor [tolerance=±5% resistance=220 package=THT]
  Power_plug1 = Power plug

nets:
  N1: T1.+Vs, Componente1.5V
  N2: T1.Vout, Componente1.A1
  GND: T1.GND, Componente1.GND, LED1.cathode
  N3: Componente1.D9_PWM, R1.Pin_1
  N4: LED1.anode, R1.Pin_0
  GND_2: Componente3.GND, T2.GND, LED2.cathode, Power_plug1.GND
  N5: Componente3.RAW, Power_plug1.VCC
  N6: Componente3.VCC, T2.+Vs
  N7: Componente3.A1, T2.Vout
  N8: Componente3.D9_PWM, R2.Pin_1
